// Logisim project a.circ as structural Verilog: 1 circuit, main circuit TP1
module TP1 (
  input  a,
  input  e0,
  input  b,
  input  e1,
  input  i,
  input  y,
  input  e0_2,
  input  i_2,
  input  e0_3,
  input  a_2,
  input  b_2,
  input  e0_4,
  input  i_3,
  input  e0_5,
  output out_15,
  output out_16,
  output out_17,
  output out_18,
  output out_19
);

  wire and_2_out, and_3_out, and_4_out, and_5_out, and_6_out, and_7_out, not_1_out, not_2_out, not_3_out,
       not_4_out, not_5_out;

  not not_1 (not_1_out, b);
  not not_2 (not_2_out, i_2);
  not not_3 (not_3_out, b_2);
  not not_4 (not_4_out, a_2);
  and and_1 (out_15, a, not_1_out);
  and and_2 (and_2_out, e0_2, not_2_out);
  and and_3 (and_3_out, i_2, e0_3);
  and and_4 (and_4_out, a_2, not_3_out);
  and and_5 (and_5_out, b_2, not_4_out);
  not not_5 (not_5_out, i_3);
  or or_1 (out_17, and_2_out, and_3_out);
  or or_2 (out_18, and_4_out, and_5_out);
  and and_6 (and_6_out, e0_4, not_5_out);
  and and_7 (and_7_out, i_3, e0_5);
  or or_3 (out_19, and_6_out, and_7_out);
  Multiplexer multiplexer_1 (.in0(e0), .in1(e1), .out(out_16), .sel(i), .en(y));

  // Notes on the sheet:
  //   A et non B
  //   Multiplexeur a 2 entree ver 1
  //   Fonction xor
  //   Multiplexeur a 2 entrée ver 2
endmodule
