// Logisim project add4b.circ as structural Verilog: 1 circuit, main circuit main
module main (
  input  A,
  input  B,
  input  C,
  input  A_2,
  input  B_2,
  input  A_3,
  input  B_3,
  input  A_4,
  input  B_4,
  output S,
  output S_2,
  output S_3,
  output S_4
);

  wire and_1_out, and_2_out, and_3_out, and_4_out, and_5_out, and_6_out, and_7_out, and_8_out, or_1_out,
       or_2_out, or_3_out, xor_1_out, xor_2_out, xor_4_out, xor_5_out, xor_7_out, xor_8_out, xor_10_out,
       xor_11_out;

  xor xor_1 (xor_1_out, A, B);
  xor xor_2 (xor_2_out, A, B);
  xor xor_3 (S, xor_1_out, C);
  and and_1 (and_1_out, xor_2_out, C);
  and and_2 (and_2_out, A, B);
  or or_1 (or_1_out, and_1_out, and_2_out);
  xor xor_4 (xor_4_out, A_2, B_2);
  xor xor_5 (xor_5_out, A_2, B_2);
  xor xor_6 (S_2, xor_4_out, or_1_out);
  and and_3 (and_3_out, xor_5_out, or_1_out);
  and and_4 (and_4_out, A_2, B_2);
  or or_2 (or_2_out, and_3_out, and_4_out);
  xor xor_7 (xor_7_out, A_3, B_3);
  xor xor_8 (xor_8_out, A_3, B_3);
  and and_5 (and_5_out, xor_7_out, or_2_out);
  and and_6 (and_6_out, A_3, B_3);
  xor xor_9 (S_3, xor_8_out, or_2_out);
  xor xor_10 (xor_10_out, A_4, B_4);
  or or_3 (or_3_out, and_5_out, and_6_out);
  xor xor_11 (xor_11_out, A_4, B_4);
  and and_7 (and_7_out, xor_10_out, or_3_out);
  and and_8 (and_8_out, A_4, B_4);
  xor xor_12 (S_4, xor_11_out, or_3_out);
  // OR_Gate or_4 has open pins: in0=and_7_out, in1=and_8_out, out=open
endmodule
